// Logisim project C023-Dhaval Mehta_DLD Mini Project.circ as structural Verilog: 5 circuits, main circuit main
module main (
);

  wire and_1_out, and_2_out, and_3_out, button_1_out, button_2_out, button_3_out, clock_1_out,
       difffordisplay_1_o1, difffordisplay_1_o2, difffordisplay_1_o3, difffordisplay_1_o4,
       difffordisplay_1_t1, difffordisplay_1_t2, difffordisplay_1_t3, difffordisplay_1_t4,
       doubledabble_1_out_13, doubledabble_1_out_14, doubledabble_1_out_15, doubledabble_1_out_16,
       doubledabble_1_out_17, doubledabble_1_out_18, doubledabble_1_out_19, doubledabble_1_out_20,
       doubledabble_2_out_13, doubledabble_2_out_14, doubledabble_2_out_15, doubledabble_2_out_16,
       doubledabble_2_out_17, doubledabble_2_out_18, doubledabble_2_out_19, doubledabble_2_out_20,
       Left_2_a_2, Left_2_b_2, Left_2_c_2, Left_2_d_2, Left_2_e, Left_2_f, Left_2_g, Left_3_a_2, Left_3_b_2,
       Left_3_c_2, Left_3_d_2, Left_3_e, Left_3_f, Left_3_g, Left_a_2, Left_b_2, Left_c_2, Left_d_2, Left_e,
       Left_f, Left_g, not_1_out, not_2_out, not_3_out, not_4_out, not_5_out, not_6_out, or_1_out, or_2_out,
       or_3_out, Right_2_a_2, Right_2_b_2, Right_2_c_2, Right_2_d_2, Right_2_e, Right_2_f, Right_2_g,
       Right_3_a_2, Right_3_b_2, Right_3_c_2, Right_3_d_2, Right_3_e, Right_3_f, Right_3_g, Right_a_2,
       Right_b_2, Right_c_2, Right_d_2, Right_e, Right_f, Right_g, t_ff_1_q, t_ff_2_q, t_ff_3_q, t_ff_4_q,
       t_ff_5_q, t_ff_6_q, t_ff_7_q, t_ff_8_q, t_ff_9_q, t_ff_10_q, t_ff_11_q, t_ff_12_q, t_ff_13_q,
       t_ff_14_q, t_ff_15_q, t_ff_16_q;

  Clock clock_1 (.out(clock_1_out));
  Button button_1 (.out(button_1_out));
  or or_1 (or_1_out, clock_1_out, button_1_out);
  Button button_2 (.out(button_2_out));
  Button button_3 (.out(button_3_out));
  or or_2 (or_2_out, t_ff_14_q, button_2_out);
  T_Flip_Flop #(.trigger("falling")) t_ff_1 (
    .clk(or_1_out), .T(1'b1), .Q(t_ff_1_q), .reset(and_2_out));  // open: Qn, preset, en
  or or_3 (or_3_out, t_ff_16_q, button_3_out);
  T_Flip_Flop #(.trigger("falling")) t_ff_2 (
    .clk(t_ff_1_q), .T(1'b1), .Q(t_ff_2_q), .reset(and_2_out));  // open: Qn, preset, en
  T_Flip_Flop #(.trigger("falling")) t_ff_3 (
    .clk(or_2_out), .T(1'b1), .Q(t_ff_3_q), .reset(and_3_out));  // open: Qn, preset, en
  T_Flip_Flop #(.trigger("falling")) t_ff_4 (
    .clk(or_3_out), .T(1'b1), .Q(t_ff_4_q), .reset(and_1_out));  // open: Qn, preset, en
  T_Flip_Flop #(.trigger("falling")) t_ff_5 (
    .clk(t_ff_2_q), .T(1'b1), .Q(t_ff_5_q), .reset(and_2_out));  // open: Qn, preset, en
  T_Flip_Flop #(.trigger("falling")) t_ff_6 (
    .clk(t_ff_3_q), .T(1'b1), .Q(t_ff_6_q), .reset(and_3_out));  // open: Qn, preset, en
  T_Flip_Flop #(.trigger("falling")) t_ff_7 (
    .clk(t_ff_4_q), .T(1'b1), .Q(t_ff_7_q), .reset(and_1_out));  // open: Qn, preset, en
  not not_1 (not_1_out, 1'b1);
  T_Flip_Flop #(.trigger("falling")) t_ff_8 (
    .clk(t_ff_5_q), .T(1'b1), .Q(t_ff_8_q), .reset(and_2_out));  // open: Qn, preset, en
  T_Flip_Flop #(.trigger("falling")) t_ff_9 (
    .clk(t_ff_6_q), .T(1'b1), .Q(t_ff_9_q), .reset(and_3_out));  // open: Qn, preset, en
  T_Flip_Flop #(.trigger("falling")) t_ff_10 (
    .clk(t_ff_7_q), .T(1'b1), .Q(t_ff_10_q), .reset(and_1_out));  // open: Qn, preset, en
  T_Flip_Flop #(.trigger("falling")) t_ff_11 (
    .clk(t_ff_8_q), .T(1'b1), .Q(t_ff_11_q), .reset(and_2_out));  // open: Qn, preset, en
  not not_2 (not_2_out, 1'b1);
  T_Flip_Flop #(.trigger("falling")) t_ff_12 (
    .clk(t_ff_9_q), .T(1'b1), .Q(t_ff_12_q), .reset(and_3_out));  // open: Qn, preset, en
  T_Flip_Flop #(.trigger("falling")) t_ff_13 (
    .clk(t_ff_10_q), .T(1'b1), .Q(t_ff_13_q), .reset(and_1_out));  // open: Qn, preset, en
  T_Flip_Flop #(.trigger("falling")) t_ff_14 (
    .clk(t_ff_11_q), .T(1'b1), .Q(t_ff_14_q), .reset(and_2_out));  // open: Qn, preset, en
  T_Flip_Flop #(.trigger("falling")) t_ff_15 (
    .clk(t_ff_12_q), .T(1'b1), .Q(t_ff_15_q), .reset(and_3_out));  // open: Qn, preset, en
  and and_1 (and_1_out, t_ff_4_q, t_ff_10_q, t_ff_13_q);
  DoubleDabble doubledabble_1 (
    .Inputs(not_1_out), .in_2(not_1_out), .in_3(t_ff_14_q), .in_4(t_ff_11_q), .in_5(t_ff_8_q),
    .in_6(t_ff_5_q), .in_7(t_ff_2_q), .in_8(t_ff_1_q), .out_13(doubledabble_1_out_13),
    .out_14(doubledabble_1_out_14), .out_15(doubledabble_1_out_15), .out_16(doubledabble_1_out_16),
    .out_17(doubledabble_1_out_17), .out_18(doubledabble_1_out_18), .out_19(doubledabble_1_out_19),
    .out_20(doubledabble_1_out_20));  // open: out_9, out_10, out_11, out_12
  not not_3 (not_3_out, t_ff_2_q);
  not not_4 (not_4_out, t_ff_1_q);
  T_Flip_Flop #(.trigger("falling")) t_ff_16 (
    .clk(t_ff_15_q), .T(1'b1), .Q(t_ff_16_q), .reset(and_3_out));  // open: Qn, preset, en
  DiffForDisplay difffordisplay_1 (
    .A(t_ff_13_q), .B(t_ff_10_q), .C(t_ff_7_q), .D(t_ff_4_q), .T1(difffordisplay_1_t1),
    .T2(difffordisplay_1_t2), .T3(difffordisplay_1_t3), .T4(difffordisplay_1_t4), .O1(difffordisplay_1_o1),
    .O2(difffordisplay_1_o2), .O3(difffordisplay_1_o3), .O4(difffordisplay_1_o4));
  and and_2 (and_2_out, not_4_out, not_3_out, t_ff_5_q, t_ff_8_q, t_ff_11_q, t_ff_14_q);
  DoubleDabble doubledabble_2 (
    .Inputs(not_2_out), .in_2(not_2_out), .in_3(t_ff_16_q), .in_4(t_ff_15_q), .in_5(t_ff_12_q),
    .in_6(t_ff_9_q), .in_7(t_ff_6_q), .in_8(t_ff_3_q), .out_13(doubledabble_2_out_13),
    .out_14(doubledabble_2_out_14), .out_15(doubledabble_2_out_15), .out_16(doubledabble_2_out_16),
    .out_17(doubledabble_2_out_17), .out_18(doubledabble_2_out_18), .out_19(doubledabble_2_out_19),
    .out_20(doubledabble_2_out_20));  // open: out_9, out_10, out_11, out_12
  not not_5 (not_5_out, t_ff_6_q);
  not not_6 (not_6_out, t_ff_3_q);
  and and_3 (and_3_out, not_6_out, not_5_out, t_ff_9_q, t_ff_12_q, t_ff_15_q, t_ff_16_q);
  BinaryTo7Seg Left (
    .A(doubledabble_1_out_13), .B(doubledabble_1_out_14), .C(doubledabble_1_out_15),
    .D(doubledabble_1_out_16), .a_2(Left_a_2), .b_2(Left_b_2), .c_2(Left_c_2), .d_2(Left_d_2), .e(Left_e),
    .f(Left_f), .g(Left_g));
  BinaryTo7Seg Right (
    .A(doubledabble_1_out_17), .B(doubledabble_1_out_18), .C(doubledabble_1_out_19),
    .D(doubledabble_1_out_20), .a_2(Right_a_2), .b_2(Right_b_2), .c_2(Right_c_2), .d_2(Right_d_2),
    .e(Right_e), .f(Right_f), .g(Right_g));
  BinaryTo7Seg Left_2 (
    .A(doubledabble_2_out_13), .B(doubledabble_2_out_14), .C(doubledabble_2_out_15),
    .D(doubledabble_2_out_16), .a_2(Left_2_a_2), .b_2(Left_2_b_2), .c_2(Left_2_c_2), .d_2(Left_2_d_2),
    .e(Left_2_e), .f(Left_2_f), .g(Left_2_g));
  BinaryTo7Seg Right_2 (
    .A(doubledabble_2_out_17), .B(doubledabble_2_out_18), .C(doubledabble_2_out_19),
    .D(doubledabble_2_out_20), .a_2(Right_2_a_2), .b_2(Right_2_b_2), .c_2(Right_2_c_2), .d_2(Right_2_d_2),
    .e(Right_2_e), .f(Right_2_f), .g(Right_2_g));
  BinaryTo7Seg Left_3 (
    .A(difffordisplay_1_t1), .B(difffordisplay_1_t2), .C(difffordisplay_1_t3), .D(difffordisplay_1_t4),
    .a_2(Left_3_a_2), .b_2(Left_3_b_2), .c_2(Left_3_c_2), .d_2(Left_3_d_2), .e(Left_3_e), .f(Left_3_f),
    .g(Left_3_g));
  BinaryTo7Seg Right_3 (
    .A(difffordisplay_1_o1), .B(difffordisplay_1_o2), .C(difffordisplay_1_o3), .D(difffordisplay_1_o4),
    .a_2(Right_3_a_2), .b_2(Right_3_b_2), .c_2(Right_3_c_2), .d_2(Right_3_d_2), .e(Right_3_e), .f(Right_3_f),
    .g(Right_3_g));
  _7_Segment_Display u_7_segment_display_1 (
    .g(Left_3_g), .f(Left_3_f), .a(Left_3_a_2), .b(Left_3_b_2), .e(Left_3_e), .d(Left_3_d_2), .c(Left_3_c_2));  // open: dp
  _7_Segment_Display u_7_segment_display_2 (
    .g(Right_3_g), .f(Right_3_f), .a(Right_3_a_2), .b(Right_3_b_2), .e(Right_3_e), .d(Right_3_d_2),
    .c(Right_3_c_2));  // open: dp
  _7_Segment_Display u_7_segment_display_3 (
    .g(Left_2_g), .f(Left_2_f), .a(Left_2_a_2), .b(Left_2_b_2), .e(Left_2_e), .d(Left_2_d_2), .c(Left_2_c_2));  // open: dp
  _7_Segment_Display u_7_segment_display_4 (
    .g(Right_2_g), .f(Right_2_f), .a(Right_2_a_2), .b(Right_2_b_2), .e(Right_2_e), .d(Right_2_d_2),
    .c(Right_2_c_2));  // open: dp
  _7_Segment_Display u_7_segment_display_5 (
    .g(Left_g), .f(Left_f), .a(Left_a_2), .b(Left_b_2), .e(Left_e), .d(Left_d_2), .c(Left_c_2));  // open: dp
  _7_Segment_Display u_7_segment_display_6 (
    .g(Right_g), .f(Right_f), .a(Right_a_2), .b(Right_b_2), .e(Right_e), .d(Right_d_2), .c(Right_c_2));  // open: dp
endmodule

module BinaryTo7Seg (
  input  A,
  input  B,
  input  C,
  input  D,
  output a_2,
  output b_2,
  output c_2,
  output d_2,
  output e,
  output f,
  output g
);

  wire and_1_out, and_2_out, and_3_out, and_4_out, and_5_out, and_6_out, and_7_out, and_8_out, and_9_out,
       and_10_out, and_11_out, and_12_out, and_13_out, and_14_out, and_15_out, and_16_out, and_17_out,
       not_1_out, not_2_out, not_3_out, not_4_out, not_5_out, not_6_out, not_7_out, not_8_out, not_9_out,
       not_10_out, not_11_out, not_12_out, not_13_out, not_14_out, not_15_out, not_16_out, not_17_out,
       not_18_out, not_19_out, not_20_out, not_21_out, or_1_out, or_2_out, or_3_out, or_4_out, or_6_out,
       or_8_out, or_9_out, or_10_out, or_11_out, or_14_out, or_15_out;

  not not_1 (not_1_out, B);
  and and_1 (and_1_out, not_1_out, not_2_out);
  not not_2 (not_2_out, D);
  and and_2 (and_2_out, B, D);
  not not_3 (not_3_out, B);
  not not_4 (not_4_out, C);
  and and_3 (and_3_out, not_4_out, not_5_out);
  not not_5 (not_5_out, D);
  not not_6 (not_6_out, C);
  or or_1 (or_1_out, not_6_out, D);
  not not_7 (not_7_out, B);
  and and_4 (and_4_out, not_7_out, not_8_out);
  not not_8 (not_8_out, D);
  not not_9 (not_9_out, B);
  and and_5 (and_5_out, not_9_out, C);
  not not_10 (not_10_out, D);
  and and_6 (and_6_out, B, not_11_out);
  not not_11 (not_11_out, C);
  not not_12 (not_12_out, B);
  and and_7 (and_7_out, not_12_out, not_13_out);
  not not_13 (not_13_out, D);
  and and_8 (and_8_out, C, not_14_out);
  not not_14 (not_14_out, D);
  not not_15 (not_15_out, C);
  and and_9 (and_9_out, not_15_out, not_16_out);
  not not_16 (not_16_out, D);
  and and_10 (and_10_out, B, not_17_out);
  not not_17 (not_17_out, C);
  and and_11 (and_11_out, B, not_18_out);
  not not_18 (not_18_out, D);
  not not_19 (not_19_out, B);
  and and_12 (and_12_out, not_19_out, C);
  and and_13 (and_13_out, B, not_20_out);
  not not_20 (not_20_out, C);
  and and_14 (and_14_out, B, not_21_out);
  not not_21 (not_21_out, D);
  or or_2 (or_2_out, and_1_out, C);
  or or_3 (or_3_out, and_2_out, A);
  or or_4 (or_4_out, not_3_out, and_3_out);
  and and_15 (and_15_out, C, D);
  or or_5 (c_2, or_1_out, B);
  or or_6 (or_6_out, and_4_out, and_5_out);
  and and_16 (and_16_out, C, not_10_out);
  and and_17 (and_17_out, and_6_out, D);
  or or_7 (e, and_7_out, and_8_out);
  or or_8 (or_8_out, and_9_out, and_10_out);
  or or_9 (or_9_out, and_11_out, A);
  or or_10 (or_10_out, and_12_out, and_13_out);
  or or_11 (or_11_out, and_14_out, A);
  or or_12 (a_2, or_2_out, or_3_out);
  or or_13 (b_2, or_4_out, and_15_out);
  or or_14 (or_14_out, or_6_out, and_16_out);
  or or_15 (or_15_out, and_17_out, A);
  or or_16 (f, or_8_out, or_9_out);
  or or_17 (g, or_10_out, or_11_out);
  or or_18 (d_2, or_14_out, or_15_out);
endmodule

module DiffForDisplay (
  input  A,
  input  B,
  input  C,
  input  D,
  output T1,
  output T2,
  output T3,
  output T4,
  output O1,
  output O2,
  output O3,
  output O4
);

  wire and_1_out, and_2_out, and_3_out, and_5_out, and_6_out, not_1_out, not_2_out, not_3_out, not_4_out;

  and and_1 (and_1_out, A, C);
  and and_2 (and_2_out, A, B);
  and and_3 (and_3_out, A, not_1_out);
  not not_1 (not_1_out, B);
  not not_2 (not_2_out, C);
  not not_3 (not_3_out, A);
  and and_4 (O2, not_3_out, B);
  not not_4 (not_4_out, A);
  and and_5 (and_5_out, not_4_out, C);
  and and_6 (and_6_out, A, B);
  or or_1 (T4, and_1_out, and_2_out);
  and and_7 (O1, and_3_out, not_2_out);
  or or_2 (O3, and_5_out, and_6_out);

  assign O4 = D;
  assign T1 = 1'b0;
  assign T2 = 1'b0;
  assign T3 = 1'b0;
endmodule

module Dabble (
  input  A,
  input  B,
  input  C,
  input  D,
  output a_2,
  output b_2,
  output c_2,
  output d_2
);

  wire and_1_out, and_2_out, and_3_out, and_4_out, and_5_out, and_6_out, and_7_out, and_8_out, and_9_out,
       and_10_out, and_11_out, and_12_out, and_13_out, not_1_out, not_2_out, not_3_out, not_4_out, not_5_out,
       not_6_out, not_7_out, not_8_out, or_1_out, or_3_out, or_6_out;

  not not_1 (not_1_out, C);
  not not_2 (not_2_out, B);
  not not_3 (not_3_out, A);
  not not_4 (not_4_out, B);
  and and_1 (and_1_out, B, D);
  or or_1 (or_1_out, and_1_out, and_2_out);
  and and_2 (and_2_out, B, C);
  and and_3 (and_3_out, B, not_1_out);
  not not_5 (not_5_out, D);
  and and_4 (and_4_out, not_2_out, C);
  and and_5 (and_5_out, C, D);
  not not_6 (not_6_out, D);
  and and_6 (and_6_out, not_3_out, not_4_out);
  and and_7 (and_7_out, B, C);
  not not_7 (not_7_out, D);
  or or_2 (a_2, or_1_out, A);
  and and_8 (and_8_out, and_3_out, not_5_out);
  and and_9 (and_9_out, A, D);
  or or_3 (or_3_out, and_4_out, and_5_out);
  and and_10 (and_10_out, A, not_6_out);
  and and_11 (and_11_out, and_6_out, D);
  and and_12 (and_12_out, and_7_out, not_7_out);
  not not_8 (not_8_out, D);
  or or_4 (b_2, and_8_out, and_9_out);
  or or_5 (c_2, or_3_out, and_10_out);
  or or_6 (or_6_out, and_11_out, and_12_out);
  and and_13 (and_13_out, A, not_8_out);
  or or_7 (d_2, or_6_out, and_13_out);
endmodule

module DoubleDabble (
  input  Inputs,
  input  in_2,
  input  in_3,
  input  in_4,
  input  in_5,
  input  in_6,
  input  in_7,
  input  in_8,
  output out_9,
  output out_10,
  output out_11,
  output out_12,
  output out_13,
  output out_14,
  output out_15,
  output out_16,
  output out_17,
  output out_18,
  output out_19,
  output out_20
);

  wire dabble_1_a_2, dabble_1_b_2, dabble_1_c_2, dabble_1_d_2, dabble_2_a_2, dabble_2_b_2, dabble_2_c_2,
       dabble_2_d_2, dabble_3_a_2, dabble_3_b_2, dabble_3_c_2, dabble_3_d_2, dabble_4_b_2, dabble_4_c_2,
       dabble_4_d_2, dabble_5_a_2, dabble_5_b_2, dabble_5_c_2, dabble_5_d_2;

  not not_1 (out_9, 1'b1);
  Dabble dabble_1 (
    .A(out_9), .B(Inputs), .C(in_2), .D(in_3), .a_2(dabble_1_a_2), .b_2(dabble_1_b_2), .c_2(dabble_1_c_2),
    .d_2(dabble_1_d_2));
  Dabble dabble_2 (
    .A(dabble_1_b_2), .B(dabble_1_c_2), .C(dabble_1_d_2), .D(in_4), .a_2(dabble_2_a_2), .b_2(dabble_2_b_2),
    .c_2(dabble_2_c_2), .d_2(dabble_2_d_2));
  Dabble dabble_3 (
    .A(dabble_2_b_2), .B(dabble_2_c_2), .C(dabble_2_d_2), .D(in_5), .a_2(dabble_3_a_2), .b_2(dabble_3_b_2),
    .c_2(dabble_3_c_2), .d_2(dabble_3_d_2));
  Dabble dabble_4 (
    .A(out_9), .B(dabble_1_a_2), .C(dabble_2_a_2), .D(dabble_3_a_2), .a_2(out_11), .b_2(dabble_4_b_2),
    .c_2(dabble_4_c_2), .d_2(dabble_4_d_2));
  Dabble dabble_5 (
    .A(dabble_3_b_2), .B(dabble_3_c_2), .C(dabble_3_d_2), .D(in_6), .a_2(dabble_5_a_2), .b_2(dabble_5_b_2),
    .c_2(dabble_5_c_2), .d_2(dabble_5_d_2));
  Dabble dabble_6 (
    .A(dabble_4_b_2), .B(dabble_4_c_2), .C(dabble_4_d_2), .D(dabble_5_a_2), .a_2(out_12), .b_2(out_13),
    .c_2(out_14), .d_2(out_15));
  Dabble dabble_7 (
    .A(dabble_5_b_2), .B(dabble_5_c_2), .C(dabble_5_d_2), .D(in_7), .a_2(out_16), .b_2(out_17), .c_2(out_18),
    .d_2(out_19));

  assign out_10 = out_9;
  assign out_20 = in_8;
endmodule
